// Digital circuit 4_Registros.dig as structural Verilog
module _4_Registros (
  input  D3,
  input  Set,
  input  D2,
  input  D1,
  input  D0,
  input  Clock,
  input  Clear,
  input  in_9,
  input  in_11,
  input  in_13,
  input  in_15,
  input  Set_2,
  input  Set_3,
  input  Out3,
  input  Out2,
  input  Out1,
  input  Out0,
  input  Clear_2,
  input  Clear_3,
  output out_8,
  output out_10,
  output out_12,
  output out_14,
  output out_17,
  output out_18,
  output out_19,
  output out_20
);

  wire d_ff_as_4_q, d_ff_as_6_q, d_ff_as_7_q, d_ff_as_8_q, In0, In1, In2, In3, Out0_t, Out1_t, Out2_t, Out3_t;

  PullDown pulldown_1 (.out(In3));
  D_FF_AS d_ff_as_1 (.Set(Set_2), .D(In3), .C(Clock), .Clr(Clear_3), .Q(out_20));  // open: nQ
  PullDown pulldown_2 (.out(In2));
  D_FF_AS d_ff_as_2 (.Set(Set_2), .D(In2), .C(Clock), .Clr(Clear_3), .Q(out_19));  // open: nQ
  PullDown pulldown_3 (.out(In1));
  D_FF_AS d_ff_as_3 (.Set(Set_2), .D(In1), .C(Clock), .Clr(Clear_3), .Q(out_18));  // open: nQ
  D_FF_AS d_ff_as_4 (.Set(Set), .D(D3), .C(Clock), .Clr(Clear), .Q(d_ff_as_4_q));  // open: nQ
  assign out_14 = ~d_ff_as_4_q ? Out3_t : 1'bz;  // DriverInvSel driverinvsel_1
  PullDown pulldown_4 (.out(In0));
  assign In3 = d_ff_as_4_q ? in_15 : 1'bz;  // Driver driver_1
  D_FF_AS d_ff_as_5 (.Set(Set_2), .D(In0), .C(Clock), .Clr(Clear_3), .Q(out_17));  // open: nQ
  D_FF_AS d_ff_as_6 (.Set(Set), .D(D2), .C(Clock), .Clr(Clear), .Q(d_ff_as_6_q));  // open: nQ
  assign out_12 = ~d_ff_as_6_q ? Out2_t : 1'bz;  // DriverInvSel driverinvsel_2
  assign In2 = d_ff_as_6_q ? in_13 : 1'bz;  // Driver driver_2
  D_FF_AS d_ff_as_7 (.Set(Set), .D(D1), .C(Clock), .Clr(Clear), .Q(d_ff_as_7_q));  // open: nQ
  assign out_10 = ~d_ff_as_7_q ? Out1_t : 1'bz;  // DriverInvSel driverinvsel_3
  assign In1 = d_ff_as_7_q ? in_11 : 1'bz;  // Driver driver_3
  D_FF_AS d_ff_as_8 (.Set(Set), .D(D0), .C(Clock), .Clr(Clear), .Q(d_ff_as_8_q));  // open: nQ
  D_FF_AS d_ff_as_9 (.Set(Set_3), .D(Out3), .C(Clock), .Clr(Clear_2), .Q(Out3_t));  // open: nQ
  assign out_8 = ~d_ff_as_8_q ? Out0_t : 1'bz;  // DriverInvSel driverinvsel_4
  assign In0 = d_ff_as_8_q ? in_9 : 1'bz;  // Driver driver_4
  D_FF_AS d_ff_as_10 (.Set(Set_3), .D(Out2), .C(Clock), .Clr(Clear_2), .Q(Out2_t));  // open: nQ
  D_FF_AS d_ff_as_11 (.Set(Set_3), .D(Out1), .C(Clock), .Clr(Clear_2), .Q(Out1_t));  // open: nQ
  D_FF_AS d_ff_as_12 (.Set(Set_3), .D(Out0), .C(Clock), .Clr(Clear_2), .Q(Out0_t));  // open: nQ

  // Other names for the same wires on the sheet: ClrIn = Clear_3; ClrOut = Clear_2

  // Notes on the sheet:
  //   Entradas
  //   Usamos una resistencia en pull down
  //   para evitar cambios de estado arbitrarios
  //   Podemos visualizar el Out si está habilitado como 1, si es 0 no se visualiza
  //   Registros
  //   Control de la dirección del estado
  //   0 para salidas, 1 para entradas
  //   Salidas
  //   Se establece el pin Dx como salida, si es 1, si es 0 esta deshabilitado
endmodule
